# Fritzing sketch FireTruck (saved by Fritzing 1.0.5)
breadboards: 1

parts:
  Part1 = Arduino Uno (Rev3) - ICSP
  Part3 = NRF24L01+ Breakout Board
  Part4 = NRF24L01+ Breakout Board  # not connected
  L298N1 = L298N DC motor driver
  M1 = DC Motor [voltage_(max)=6V voltage_(min)=3V]  # not connected
  M2 = DC Motor [voltage_(max)=6V voltage_(min)=3V]  # not connected
  Part5 = Thumb Joystick
  BAT1 = LIPO-1000mAh [package=lipo-1000]
  BAT2 = LIPO-1000mAh [package=lipo-1000]
  R1 = Resistor [tolerance=±5% power=0.25W resistance=15k package=THT]  # not connected
  R2 = Resistor [tolerance=±5% power=0.25W resistance=10k package=THT]  # not connected
  LED1 = LED - 3mm [color="White (4500K)" current=0.030A package="3 mm [THT]"]
  LED2 = LED - 3mm [color="White (4500K)" current=0.030A package="3 mm [THT]"]
  LED3 = LED - 3mm [color="Blue (505nm)" current=0.030A package="3 mm [THT]"]
  LED4 = LED - 3mm [color="Blue (505nm)" current=0.030A package="3 mm [THT]"]
  LED5 = LED - 3mm [color="Red (660nm)" current=0.030A package="3 mm [THT]"]
  LED6 = LED - 3mm [color="Red (660nm)" current=0.030A package="3 mm [THT]"]
  R3 = Resistor [tolerance=±5% power=0.25W resistance=220 package=THT]
  R4 = Resistor [tolerance=±5% power=0.25W resistance=220 package=THT]
  R5 = Resistor [tolerance=±5% power=0.25W resistance=220 package=THT]
  R6 = Resistor [tolerance=±5% power=0.25W resistance=220 package=THT]
  R7 = Resistor [tolerance=±5% power=0.25W resistance=220 package=THT]
  R8 = Resistor [tolerance=±5% power=0.25W resistance=220 package=THT]
  Part6 = Arduino Mega 2560 (Rev3)

nets:
  N1: Part1.A0, Part5.VERT
  N2: Part1.A1, Part5.SEL
  N3: Part1.ICSP_MOSI, Part1.D11_PWM/MOSI, Part3.MOSI
  N4: Part1.D8, Part3.CS
  N5: Part1.D12/MISO, Part3.MISO
  N6: Part1.D13/SCK, Part3.SCK
  GND: Part1.GND, Part3.GND, Part5.GND
  N7: Part1.D2, Part5.HORZ
  N8: Part1.D7, Part3.CE
  3V3: Part1.3V3, Part3.VCC
  5V: Part1.5V, Part5.VCC
  N9: L298N1.12V, BAT1.+
  N10: L298N1.GND, BAT2.-
  N11: L298N1.5V#9, L298N1.ENA
  N12: L298N1.5V#10, L298N1.ENB
  N13: BAT1.-, BAT2.+
  N14: LED1.cathode, Part6.D22
  N15: LED1.anode, R3.Pin_0
  N16: LED2.cathode, Part6.D23
  N17: LED2.anode, R4.Pin_0
  N18: LED3.cathode, Part6.D24
  N19: LED3.anode, R5.Pin_0
  N20: LED4.cathode, Part6.D25
  N21: LED4.anode, R6.Pin_0
  N22: LED5.anode, R7.Pin_0
  N23: LED6.anode, R8.Pin_0
  N24: R3.Pin_1, R4.Pin_1, R5.Pin_1, R6.Pin_1, R7.Pin_1, R8.Pin_1

custom parts:
  L298N DC motor driver: 2x DC motor driver with 78M05 positive voltage regulator (7..35 V) L298N: max 46 V, 2 A Set 5 V Enable jumper to enable 5 V regultor (needed for the L298N) and +5 V output at screw terminal or supply external +5 V at screw terminal Set ENA and/or ENB to +5 V to enable motor permanently or supply ENA and/or ENB with PWM signal IN1 and IN2 set rotation directory for motor A (OUT1/OUT2) IN2 and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
